# Fritzing sketch billow.b (saved by Fritzing 1.0.3b)
circuit board: 10cm x 4.49999cm
breadboards: 1

parts:
  2K1 = Rotary Potentiometer (Small) [maximum_resistance=2kΩ knob_status=50% power=0.5W package=THT]
  S17 = Tactile switch 12mm [package=THT]
  2K2 = Rotary Potentiometer (Small) [maximum_resistance=2kΩ knob_status=50% power=0.5W package=THT]
  S18 = Tactile switch 12mm [package=THT]
  2K3 = Rotary Potentiometer (Small) [maximum_resistance=2kΩ knob_status=50% power=0.5W package=THT]
  2K4 = Rotary Potentiometer (Small) [maximum_resistance=2kΩ knob_status=50% power=0.5W package=THT]
  S19 = Tactile switch 12mm [package=THT]
  S20 = Tactile switch 12mm [package=THT]
  2K5 = Rotary Potentiometer (Small) [maximum_resistance=2kΩ knob_status=50% power=0.5W package=THT]
  S21 = Tactile switch 12mm [package=THT]
  S22 = SPST Switch [package=switch-spdt_lock.007s]
  6N137 = IC, DIP package, 8 pins [chip_label=IC]
  J4 = 3.5mm Audio Jack-wq-pj320b.fzpz [package=audio-jack-3.5mm-smd]
  J3 = female pin header, 4 pins [form="♀ (female)"]
  S24 = SPST Switch [package=switch-spdt_lock.007s]
  S25 = SWITCH-DPDT-latching [package=os]
  J5 = female pin header, 4 pins [form="♀ (female)"]
  A1 = Waveshare rp2040-zero tht [package=THT]
  4_7k = Resistor [tolerance=±5% power=0.25W resistance=4.7k package=THT]
  220 = Resistor [tolerance=±5% power=0.25W resistance=220 package=THT]
  D4148 = Diode [package=diode-1n4148]
  104 = Ceramic Capacitor [capacitance=100nF voltage=35V package="200 mil [THT, multilayer]"]
  9110 = IC, DIP package, 8 pins [chip_label=IC]

nets:
  N1: 2K1.leg1, S17.3, S17.4
  N2: 2K1.wiper, 2K2.wiper, 2K3.wiper, 2K4.wiper, 2K5.wiper, J3.pin3
  N3: S17.1, S17.2, S18.1, S18.2, S19.1, S19.2, S20.1, S20.2, S21.1, S21.2, S22.P, J3.pin4
  N4: 2K2.leg1, S18.3, S18.4
  N5: 2K3.leg1, S19.3, S19.4
  N6: 2K4.leg1, S20.3, S20.4
  N7: 2K5.leg1, S21.3, S21.4, S22.O
  N8: 6N137.pin2, 220.Pin_0, D4148.C
  N9: 6N137.pin3, J4.Pin_3, A1.Pin_12, D4148.A
  GND: 6N137.pin5, J4.pin_4, J3.pin1, A1.Pin_2, A1.Pin_11, 104.1, 9110.pin5, 9110.pin8
  N10: 6N137.pin6, A1.Pin_22, 4_7k.Pin_1
  N11: 6N137.pin8, A1.Pin_3, A1.Pin_10, 4_7k.Pin_0, 104.0
  N12: J4.pin_2, 220.Pin_1
  N13: J3.pin2, S24.P
  N14: S24.O, A1.Pin_1, 9110.pin2, 9110.pin3
  N15: S25.1, J5.pin1
  N16: S25.2, J5.pin2
  N17: S25.3, A1.Pin_14, 9110.pin4
  N18: S25.4, A1.Pin_13, 9110.pin1
  N19: S25.5, J5.pin3
  N20: S25.6, J5.pin4
  N21: A1.Pin_5, 9110.pin7
  N22: A1.Pin_6, 9110.pin6

notes:
  jlcjlcjlcjlc
  blueprint@poetaster.de 2024
  midi billow
  + i/0 | - i/0
  5v -/+ | r1/2

custom parts:
  Tactile switch 12mm: 12 mm tactile switch (push button/momentary switch) from the B3F family.
  3.5mm Audio Jack-wq-pj320b.fzpz: 3.5mm Audio Jack WQP-PJ320B is a SMD jack, dia 1/8 inch, female, right angle and through hole.
  SWITCH-DPDT-latching: DPDT latching pushbutton switch
  Waveshare rp2040-zero tht: .RP2040-Zero, A Low-Cost, High-Performance Pico-Like MCU Board Based On Raspberry Pi Microcontroller RP2040. This varant is THT without the extra connections.
